// Digital circuit FSM.dig as structural Verilog
module FSM (
  input  [3:0] op,
  input  clk
);

  wire dipswitch_1_out;
  wire [2:0] counter_1_out;
  wire [3:0] jcmp_out;
  wire [7:0] FSM_0_d, FSM_1_d, FSM_2_d;

  DipSwitch dipswitch_1 (.out(dipswitch_1_out));
  Counter #(.Bits(3)) counter_1 (.en(1'b1), .C(clk), .clr(dipswitch_1_out), .out(counter_1_out));  // open: ovf
  DipSwitch jcmp (.out(jcmp_out[0]));
  DipSwitch interrupt (.out(jcmp_out[1]));
  DipSwitch reset (.out(jcmp_out[2]));
  DipSwitch op2 (.out(jcmp_out[3]));
  EEPROM #(.AddrBits(12), .Bits(8)) FSM_0 (
    .A({1'b0, op, counter_1_out, jcmp_out}), .CS(1'b1), .WE(1'b0), .OE(1'b1), .D(FSM_0_d));
  EEPROM #(.AddrBits(12), .Bits(8)) FSM_1 (
    .A({1'b0, op, counter_1_out, jcmp_out}), .CS(1'b1), .WE(1'b0), .OE(1'b1), .D(FSM_1_d));
  EEPROM #(.AddrBits(12), .Bits(8)) FSM_2 (
    .A({1'b0, op, counter_1_out, jcmp_out}), .CS(1'b1), .WE(1'b0), .OE(1'b1), .D(FSM_2_d));
  LED Edata (.in(FSM_0_d[1]));
  LED Epc (.in(FSM_0_d[3]));
  LED Edip (.in(FSM_0_d[5]));
  LED Cir (.in(FSM_0_d[7]));
  LED sel_1 (.in(FSM_1_d[1]));
  LED E_rx (.in(FSM_1_d[3]));
  LED Cr_all (.in(FSM_1_d[5]));
  LED C_p1 (.in(FSM_1_d[7]));
  LED pcinc (.in(FSM_2_d[1]));
  LED Ccmp (.in(FSM_2_d[3]));
  LED Cstack (.in(FSM_2_d[5]));
  LED csp (.in(FSM_2_d[7]));
  LED C_p0 (.in(FSM_0_d[0]));
  LED Cdata (.in(FSM_0_d[2]));
  LED Cpc (.in(FSM_0_d[4]));
  LED Cmar (.in(FSM_0_d[6]));
  LED csp_plus__plus (.in(FSM_1_d[0]));
  LED sel_0 (.in(FSM_1_d[2]));
  LED C_rx (.in(FSM_1_d[4]));
  LED Ealu (.in(FSM_1_d[6]));
  LED NULL (.in(FSM_2_d[0]));
  LED setsub (.in(FSM_2_d[2]));
  LED Estack (.in(FSM_2_d[4]));
  LED Einstr (.in(FSM_2_d[6]));

  // Notes on the sheet:
  //   contents of FSM_0 (hex, n*v repeats v):
  //   80,80,8,8,4*d0,80,80,8,8,4*d0,1,1,6*0,1,1,8*0,30,30,6*0,30,30
  //   ,84*0,80,80,8,8,4*d0,80,80,8,8,4*d0,18*0,30,30,6*0,30,30,84*0
  //   ,80,80,8,8,4*d0,80,80,8,8,4*d0,40,40,6*0,40,40,6*0,4,4,30,30,4*0
  //   ,4,4,30,30,84*0,80,80,8,8,4*d0,80,80,8,8,4*d0,40,40,6*0,40,40
  //   ,6*0,2,2,30,30,4*0,2,2,30,30,84*0,80,80,8,8,4*d0,80,80,8,8,4*d0
  //   ,1,1,6*0,1,1,8*0,30,30,6*0,30,30,84*0,80,80,8,8,4*d0,80,80,8,8
  //   ,4*d0,1,1,6*0,1,1,8*0,30,30,6*0,30,30,84*0,80,80,8,8,4*d0,80,80
  //   ,8,8,4*d0,1,1,6*0,1,1,8*0,30,30,6*0,30,30,84*0,80,80,8,8,4*d0
  //   ,80,80,8,8,4*d0,1,1,6*0,1,1,8*0,30,30,6*0,30,30,84*0,80,80,8,8
  //   ,4*d0,80,80,8,8,4*d0,1,1,6*0,1,1,8*0,30,30,6*0,30,30,84*0,80,80
  //   ,8,8,4*d0,80,80,8,8,4*d0,1,1,6*0,1,1,8*0,30,30,6*0,30,30,84*0
  //   ,80,80,8,8,4*d0,80,80,8,8,4*d0,1,1,6*0,1,1,8*0,30,30,6*0,30,30
  //   ,84*0,80,80,8,8,4*d0,80,80,8,8,4*d0,1,1,6*0,1,1,8*0,30,30,6*0
  //   ,30,30,84*0,80,80,8,8,4*d0,80,80,8,8,4*d0,8*0,8,8,8*0,30,30,6*0
  //   ,30,30,84*0,80,80,8,8,4*d0,80,80,8,8,4*d0,18*0,30,30,4*0,10,10
  //   ,30,30,84*0,80,80,8,8,4*d0,80,80,8,8,4*d0,10,10,6*0,10,10,8*0
  //   ,30,30,6*0,30,30,84*0,80,80,8,8,4*d0,80,80,8,8,4*d0,17*0,10,30,30
  //   ,5*0,10,30,30
  //   contents of FSM_1 (hex, n*v repeats v):
  //   4*0,4*20,4*0,4*20,8,8,1,1,4*0,8,8,1,1,4*0,52,52,6*0,52,52,90*0
  //   ,4*20,4*0,4*20,0,0,1,1,6*0,1,1,4*0,12,12,6*0,12,12,90*0,4*20,4*0
  //   ,4*20,c,c,1,1,4*0,c,c,1,1,4*0,8,8,6*0,8,8,90*0,4*20,4*0,4*20,8,8
  //   ,1,1,4*0,8,8,1,1,4*0,12,12,6*0,12,12,90*0,4*20,4*0,4*20,8,8,1,1
  //   ,4*0,8,8,1,1,4*0,8c,8c,6*0,8c,8c,6*0,52,52,6*0,52,52,74*0,4*20
  //   ,4*0,4*20,8,8,1,1,4*0,8,8,1,1,4*0,52,52,6*0,52,52,90*0,4*20,4*0
  //   ,4*20,8,8,1,1,4*0,8,8,1,1,4*0,8c,8c,6*0,8c,8c,6*0,52,52,6*0,52,52
  //   ,74*0,4*20,4*0,4*20,8,8,1,1,4*0,8,8,1,1,4*0,8c,8c,6*0,8c,8c,6*0
  //   ,52,52,6*0,52,52,74*0,4*20,4*0,4*20,8,8,1,1,4*0,8,8,1,1,4*0,8c,8c
  //   ,6*0,8c,8c,6*0,52,52,6*0,52,52,74*0,4*20,4*0,4*20,8,8,1,1,4*0
  //   ,8,8,1,1,4*0,8c,8c,6*0,8c,8c,6*0,52,52,6*0,52,52,74*0,4*20,4*0
  //   ,4*20,8,8,1,1,4*0,8,8,1,1,4*0,52,52,6*0,52,52,90*0,4*20,4*0,4*20
  //   ,8,8,1,1,4*0,8,8,1,1,4*0,52,52,6*0,52,52,90*0,4*20,4*0,4*20,8,8
  //   ,1,1,6*0,1,1,4*0,1,1,6*0,1,1,90*0,4*20,4*0,4*20,0,0,1,1,6*0,1,1
  //   ,4*0,12,12,98*0,4*20,4*0,4*20,8,8,1,1,4*0,8,8,1,1,104*0,4*20,4*0
  //   ,4*20,c,c,1,1,4*0,c,c,1,1,5*0,8,7*0,8
  //   contents of FSM_2 (hex, n*v repeats v):
  //   40,40,20,20,4*0,40,40,20,20,8*0,4*4,4*0,4*4,16*0,6,6,4,4,4*0,6,6
  //   ,4,4,68*0,40,40,20,20,4*0,40,40,20,20,4*0,2,2,0,0,4*4,2,2,0,0
  //   ,4*4,40,40,6*0,40,40,6*0,6,6,4,4,4*0,6,6,4,4,68*0,40,40,20,20
  //   ,4*0,40,40,20,20,8*0,4*4,4*0,4*4,16*0,6,6,4,4,4*0,6,6,4,4,68*0
  //   ,40,40,20,20,4*0,40,40,20,20,8*0,4*4,4*0,4*4,16*0,6,6,4,4,4*0
  //   ,6,6,4,4,68*0,40,40,20,20,4*0,40,40,20,20,8*0,4*4,4*0,4*4,18*0
  //   ,4,4,6*0,4,4,4*0,6,6,6*0,6,6,54*0,40,40,20,20,4*0,40,40,20,20
  //   ,8*0,4*4,4*0,4*4,16*0,6,6,4,4,4*0,6,6,4,4,68*0,40,40,20,20,4*0
  //   ,40,40,20,20,8*0,4*4,4*0,4*4,18*0,4,4,6*0,4,4,4*0,6,6,6*0,6,6
  //   ,54*0,40,40,20,20,4*0,40,40,20,20,8*0,4*4,4*0,4*4,18*0,4,4,6*0
  //   ,4,4,4*0,6,6,6*0,6,6,54*0,40,40,20,20,4*0,40,40,20,20,8*0,4*4
  //   ,4*0,4*4,18*0,4,4,6*0,4,4,4*0,6,6,6*0,6,6,54*0,40,40,20,20,4*0
  //   ,40,40,20,20,8*0,4*4,4*0,4*4,18*0,4,4,6*0,4,4,4*0,6,6,6*0,6,6
  //   ,54*0,40,40,20,20,4*0,40,40,20,20,8*0,4*4,4*0,4*4,16*0,6,6,4,4
  //   ,4*0,6,6,4,4,68*0,40,40,20,20,4*0,40,40,20,20,8*0,4*4,4*0,4*4
  //   ,16*0,6,6,4,4,4*0,6,6,4,4,68*0,40,40,20,20,4*0,40,40,20,20,4*0
  //   ,20,20,0,0,4*4,20,20,0,0,4*4,16*0,6,6,4,4,4*0,6,6,4,4,68*0,40,40
  //   ,20,20,4*0,40,40,20,20,4*0,80,80,0,0,4*4,80,80,0,0,4*4,10,10,6*0
  //   ,10,10,6*0,6,6,4,4,4*0,4*4,68*0,40,40,20,20,4*0,40,40,20,20,8*0
  //   ,4*4,4*0,6*4,6*0,4,4,8*0,4,4,6*0,4,4,68*0,40,40,20,20,4*0,40,40
  //   ,20,20,4*0,8,8,0,0,4*4,8,8,0,0,4*4,6,7*0,6,8*0,4,4,4,5*0,4,4,4
endmodule
